// Logisim project MyCPU.circ as structural Verilog: 9 circuits, main circuit main
module main (
  input  reset
);

  wire alu_1_out_5, and_1_out, clock_1_out, control_1_alusrc, control_1_branch, control_1_extop,
       control_1_jump, control_1_memtoreg, control_1_memwrite, control_1_regdst, control_1_regwrite,
       n7_segment_display_1_p1, n7_segment_display_2_p3, n7_segment_display_2_p5, n7_segment_display_2_p7;
  wire [1:0] multiplexer_1_out;
  wire [3:0] control_1_aluctr;
  wire [7:0] regs_1_out_8, regs_1_out_9, regs_1_out_10, regs_1_out_11;
  wire [11:0] rom_1_data;
  wire [15:0] alu_1_out_4, exp_1_out_3, exp_2_out_3, mem_1_out_6, multiplexer_2_out, multiplexer_3_out,
       npc_1_out_8, regs_1_out_12, regs_1_out_13;
  wire [15:12] rom_1_data_2;

  Clock clock_1 (.out(clock_1_out));
  Exp exp_1 (.in_1(rom_1_data[7:0]), .Extop(and_1_out), .out_3(exp_1_out_3));
  and and_1 (and_1_out, rom_1_data[7], 1'b1);
  NPC npc_1 (
    .CLK(clock_1_out), .Reset(reset), .jump(control_1_jump), .branch(control_1_branch), .zero(alu_1_out_5),
    .in_6(exp_1_out_3), .in_7(rom_1_data), .out_8(npc_1_out_8));
  Multiplexer #(.width(2)) multiplexer_1 (
    .in0(rom_1_data[9:8]), .in1(rom_1_data[7:6]), .out(multiplexer_1_out), .sel(control_1_regdst));  // open: en
  ROM #(.addrWidth(16), .dataWidth(16)) rom_1 (.addr(npc_1_out_8), .data({rom_1_data_2, rom_1_data}));  // open: sel
  Regs regs_1 (
    .in_1(multiplexer_3_out), .RegWrite(control_1_regwrite), .reset(reset), .Ra(rom_1_data[11:10]),
    .clk(clock_1_out), .Rb(rom_1_data[9:8]), .Rw(multiplexer_1_out), .out_12(regs_1_out_12),
    .out_13(regs_1_out_13), .out_8(regs_1_out_8), .out_9(regs_1_out_9), .out_11(regs_1_out_11),
    .out_10(regs_1_out_10));
  Exp exp_2 (.in_1(rom_1_data[7:0]), .Extop(control_1_extop), .out_3(exp_2_out_3));
  Multiplexer #(.width(16)) multiplexer_2 (
    .in0(regs_1_out_13), .in1(exp_2_out_3), .out(multiplexer_2_out), .sel(control_1_alusrc));  // open: en
  ALU alu_1 (
    .in_1(regs_1_out_12), .in_2(multiplexer_2_out), .Aluctr(control_1_aluctr), .out_4(alu_1_out_4),
    .out_5(alu_1_out_5));
  Control control_1 (
    .opcode(rom_1_data_2), .funct(rom_1_data[2:0]), .ALUSrc(control_1_alusrc), .MemtoReg(control_1_memtoreg),
    .RegWrite(control_1_regwrite), .MemWrite(control_1_memwrite), .branch(control_1_branch),
    .jump(control_1_jump), .extop(control_1_extop), .ALUctr(control_1_aluctr), .Regdst(control_1_regdst));
  Mem mem_1 (
    .MenWrite(control_1_memwrite), .clk(clock_1_out), .Reset(reset), .in_2(regs_1_out_13),
    .out_6(mem_1_out_6), .in_1(alu_1_out_4));
  Multiplexer #(.width(16)) multiplexer_3 (
    .in0(alu_1_out_4), .in1(mem_1_out_6), .out(multiplexer_3_out), .sel(control_1_memtoreg));  // open: en
  // _7_Segment_Display 7_segment_display_1: pin names not known; wires that end beside it: n7_segment_display_1_p1, n7_segment_display_1_p1
  // BlockBottom blockbottom_1: pin names not known
  // BlockTop blocktop_1: pin names not known
  // _7_Segment_Display 7_segment_display_2: pin names not known; wires that end beside it: n7_segment_display_1_p1, n7_segment_display_1_p1, n7_segment_display_2_p3, n7_segment_display_2_p3, n7_segment_display_2_p5, n7_segment_display_2_p5, n7_segment_display_2_p7, n7_segment_display_2_p7
  // _7_Segment_Display 7_segment_display_3: pin names not known; wires that end beside it: n7_segment_display_1_p1, n7_segment_display_1_p1, n7_segment_display_2_p3, n7_segment_display_2_p3, n7_segment_display_2_p5, n7_segment_display_2_p5, n7_segment_display_2_p7, n7_segment_display_2_p7
  // blackbox blackbox_1: pin names not known; wires that end beside it: n7_segment_display_1_p1, regs_1_out_11, n7_segment_display_2_p3, regs_1_out_10, n7_segment_display_2_p5, regs_1_out_9, n7_segment_display_2_p7, regs_1_out_8
  // _7_Segment_Display 7_segment_display_4: pin names not known; wires that end beside it: n7_segment_display_2_p7, n7_segment_display_2_p7

  // Notes on the sheet:
  //   contents of rom_1 (hex, n*v repeats v):
  //   2055 3044 2555 3544 91ff
  //   DISP[3]
  //   DISP[1]
  //   DISP[2]
  //   DISP[2]
  //   DISP[0]
  //   Your Display Logic
  //   BlockTop
  //   BlockBottom
endmodule

module NPC (
  input  CLK,
  input  Reset,
  input  jump,
  input  branch,
  input  zero,
  input  [15:0] in_6,
  input  [11:0] in_7,
  output [15:0] out_8
);

  wire and_2_out;
  wire [15:0] adder_1_out, adder_2_out, and_1_out, multiplexer_1_out, multiplexer_2_out, or_1_out;

  Register #(.width(16)) register_1 (.D(multiplexer_2_out), .en(1'b1), .Q(out_8), .clk(CLK), .clr(Reset));
  assign and_1_out = out_8 & 16'hf000;  // AND_Gate and_1, 16 bits wide
  Adder #(.width(16)) adder_1 (.a(16'h1), .b(out_8), .out(adder_1_out), .cin(1'b0));  // open: cout
  assign or_1_out = and_1_out | {4'b0000, in_7};  // OR_Gate or_1, 16 bits wide
  Adder #(.width(16)) adder_2 (.a(adder_1_out), .b(in_6), .out(adder_2_out), .cin(1'b0));  // open: cout
  Multiplexer #(.width(16)) multiplexer_1 (
    .in0(adder_1_out), .in1(adder_2_out), .out(multiplexer_1_out), .sel(and_2_out));  // open: en
  and and_2 (and_2_out, branch, zero);
  Multiplexer #(.width(16)) multiplexer_2 (
    .in0(multiplexer_1_out), .in1(or_1_out), .out(multiplexer_2_out), .sel(jump));  // open: en

  // Notes on the sheet:
  //   16位立即数
  //   低12位
endmodule

module Regs (
  input  [15:0] in_1,
  input  RegWrite,
  input  reset,
  input  [1:0] Ra,
  input  clk,
  input  [1:0] Rb,
  input  [1:0] Rw,
  output [7:0] out_8,
  output [7:0] out_9,
  output [7:0] out_10,
  output [7:0] out_11,
  output [15:0] out_12,
  output [15:0] out_13
);

  wire and_1_out, and_2_out, and_3_out, and_4_out;
  wire [1:0] decoder_1_out0, decoder_1_out2;
  wire [15:8] register_1_q, register_2_q, register_3_q, register_4_q;

  Decoder #(.select(2)) decoder_1 (
    .out0(decoder_1_out0[0]), .out1(decoder_1_out0[1]), .out2(decoder_1_out2[0]), .out3(decoder_1_out2[1]),
    .sel(Rw));  // open: en
  Register #(.width(16)) register_1 (.D(in_1), .en(and_1_out), .Q({register_1_q, out_10}), .clk(clk), .clr(reset));
  and and_1 (and_1_out, RegWrite, decoder_1_out0[1]);
  Register #(.width(16)) register_2 (.D(in_1), .en(and_2_out), .Q({register_2_q, out_8}), .clk(clk), .clr(reset));
  and and_2 (and_2_out, RegWrite, decoder_1_out2[1]);
  Register #(.width(16)) register_3 (.D(in_1), .en(and_3_out), .Q({register_3_q, out_11}), .clk(clk), .clr(reset));
  and and_3 (and_3_out, RegWrite, decoder_1_out0[0]);
  Register #(.width(16)) register_4 (.D(in_1), .en(and_4_out), .Q({register_4_q, out_9}), .clk(clk), .clr(reset));
  and and_4 (and_4_out, RegWrite, decoder_1_out2[0]);
  Multiplexer #(.select(2), .width(16)) multiplexer_1 (
    .in0({register_3_q, out_11}), .in1({register_1_q, out_10}), .in2({register_4_q, out_9}),
    .in3({register_2_q, out_8}), .out(out_12), .sel(Ra));  // open: en
  Multiplexer #(.select(2), .width(16)) multiplexer_2 (
    .in0({register_3_q, out_11}), .in1({register_1_q, out_10}), .in2({register_4_q, out_9}),
    .in3({register_2_q, out_8}), .out(out_13), .sel(Rb));  // open: en

  // Notes on the sheet:
  //   r1
  //   r3
  //   r0
  //   r2
  //   A
  //   B
endmodule

module Exp (
  input  [7:0] in_1,
  input  Extop,
  output [15:0] out_3
);

  wire and_1_out;

  Multiplexer #(.width(16)) multiplexer_1 (
    .in0({{8{1'b0}}, in_1}), .in1({{8{1'b1}}, in_1}), .out(out_3), .sel(and_1_out));  // open: en
  and and_1 (and_1_out, in_1[7], Extop);

  // Notes on the sheet:
  //   imm8
endmodule

module ALU (
  input  [15:0] in_1,
  input  [15:0] in_2,
  input  [3:0] Aluctr,
  output [15:0] out_4,
  output out_5
);

  wire comparator_2_eq, comparator_3_eq, not_1_out;
  wire [0:0] comparator_1_lt;
  wire [15:0] adder_1_out, and_1_out, or_1_out, shifter_1_out, shifter_2_out, shifter_3_out, shifter_4_out,
       subtractor_1_out;

  assign or_1_out = in_1 | in_2;  // OR_Gate or_1, 16 bits wide
  assign and_1_out = in_1 & in_2;  // AND_Gate and_1, 16 bits wide
  Adder #(.width(16)) adder_1 (.a(in_1), .b(in_2), .out(adder_1_out));  // open: cin, cout
  Subtractor #(.width(16)) subtractor_1 (.a(in_1), .b(in_2), .out(subtractor_1_out));  // open: bin, bout
  Shifter #(.width(16)) shifter_1 (.in(in_1), .\dist (in_2[3:0]), .out(shifter_1_out));
  Shifter #(.width(16), .shift("lr")) shifter_2 (.in(in_1), .\dist (in_2[3:0]), .out(shifter_2_out));
  Shifter #(.width(16), .shift("ar")) shifter_3 (.in(in_1), .\dist (in_2[3:0]), .out(shifter_3_out));
  Comparator #(.width(16)) comparator_1 (.a(in_1), .b(in_2), .lt(comparator_1_lt[0]));  // open: gt, eq
  Comparator #(.width(16)) comparator_2 (.a(in_1), .b(in_2), .eq(comparator_2_eq));  // open: gt, lt
  Comparator #(.width(16)) comparator_3 (.a(in_1), .b(in_1), .eq(comparator_3_eq));  // open: gt, lt
  Shifter #(.width(16)) shifter_4 (.in(in_1), .\dist (4'b1000), .out(shifter_4_out));
  not not_1 (not_1_out, comparator_3_eq);
  Multiplexer #(.select(4), .width(16)) multiplexer_1 (
    .in0(or_1_out), .in1(and_1_out), .in2(adder_1_out), .in3(subtractor_1_out), .in4(shifter_1_out),
    .in5(shifter_2_out), .in6(shifter_3_out), .in7({{15{1'b0}}, comparator_1_lt[0]}), .in8(shifter_4_out),
    .out(out_4), .sel(Aluctr));  // open: in9, in10, in11, in12, in13, in14, in15, en
  Multiplexer #(.select(4)) multiplexer_2 (
    .in9(comparator_2_eq), .in10(not_1_out), .out(out_5), .sel(Aluctr));  // open: in0, in1, in2, in3, in4, in5, in6, in7, in8, in11, in12, in13, in14, in15, en

  // Notes on the sheet:
  //   A
  //   B
endmodule

module Mem (
  input  [15:0] in_1,
  input  [15:0] in_2,
  input  MenWrite,
  input  Reset,
  input  clk,
  output [15:0] out_6
);

  RAM #(.addrWidth(16), .dataWidth(16), .bus("separate")) ram_1 (
    .addr(in_1), .din(in_2), .data(out_6), .str(MenWrite), .sel(1'b1), .clk(clk), .ld(1'b1), .clr(Reset));
endmodule

module Control (
  input  [3:0] opcode,
  input  [2:0] funct,
  output ALUSrc,
  output MemtoReg,
  output RegWrite,
  output MemWrite,
  output branch,
  output jump,
  output extop,
  output [3:0] ALUctr,
  output Regdst
);

  wire and_2_out, and_3_out, and_4_out, and_7_out, and_8_out, and_10_out, and_11_out, and_12_out, and_13_out,
       comparator_1_eq, not_1_out, not_2_out, not_3_out, not_4_out, not_5_out, not_6_out, not_7_out,
       not_8_out, not_9_out, not_10_out, not_11_out, not_12_out, not_13_out, not_14_out, not_15_out,
       not_16_out, not_17_out, not_18_out, not_19_out, or_4_out, or_5_out, or_6_out;

  Comparator #(.width(4)) comparator_1 (.a(opcode), .b(4'b0000), .eq(comparator_1_eq));  // open: gt, lt
  or or_1 (ALUSrc, opcode[0], opcode[1], opcode[2]);
  and and_1 (MemtoReg, opcode[2], opcode[1], not_1_out);
  not not_1 (not_1_out, opcode[0]);
  not not_2 (not_2_out, opcode[3]);
  and and_2 (and_2_out, not_2_out, not_3_out);
  not not_3 (not_3_out, opcode[2]);
  not not_4 (not_4_out, opcode[3]);
  and and_3 (and_3_out, not_4_out, not_5_out);
  not not_5 (not_5_out, opcode[1]);
  not not_6 (not_6_out, opcode[3]);
  and and_4 (and_4_out, not_6_out, not_7_out);
  not not_7 (not_7_out, opcode[0]);
  and and_5 (MemWrite, opcode[2], opcode[1], opcode[0]);
  not not_8 (not_8_out, opcode[1]);
  and and_6 (jump, opcode[3], not_8_out, not_9_out);
  not not_9 (not_9_out, opcode[0]);
  not not_10 (not_10_out, opcode[1]);
  and and_7 (and_7_out, not_10_out, not_11_out);
  not not_11 (not_11_out, opcode[0]);
  and and_8 (and_8_out, opcode[2], opcode[1]);
  not not_12 (not_12_out, opcode[2]);
  not not_13 (not_13_out, opcode[1]);
  and and_9 (Regdst, not_12_out, not_13_out, not_14_out);
  not not_14 (not_14_out, opcode[0]);
  not not_15 (not_15_out, opcode[1]);
  and and_10 (and_10_out, not_15_out, opcode[0]);
  not not_16 (not_16_out, opcode[1]);
  and and_11 (and_11_out, not_16_out, not_17_out);
  not not_17 (not_17_out, opcode[0]);
  and and_12 (and_12_out, opcode[2], opcode[1]);
  not not_18 (not_18_out, opcode[2]);
  and and_13 (and_13_out, not_18_out, not_19_out);
  not not_19 (not_19_out, opcode[0]);
  or or_2 (RegWrite, and_2_out, and_3_out, and_4_out);
  or or_3 (extop, and_7_out, and_8_out, opcode[3]);
  or or_4 (or_4_out, and_10_out, opcode[3]);
  or or_5 (or_5_out, and_11_out, and_12_out);
  or or_6 (or_6_out, and_13_out, opcode[3]);
  Multiplexer multiplexer_1 (.in0(funct[0]), .in1(or_4_out), .out(ALUctr[0]), .sel(comparator_1_eq));  // open: en
  Multiplexer multiplexer_2 (.in0(funct[1]), .in1(or_5_out), .out(ALUctr[1]), .sel(comparator_1_eq));  // open: en
  Multiplexer multiplexer_3 (.in0(funct[2]), .in1(1'b0), .out(ALUctr[2]), .sel(comparator_1_eq));  // open: en
  Multiplexer multiplexer_4 (.in0(or_6_out), .in1(1'b0), .out(ALUctr[3]), .sel(comparator_1_eq));  // open: en

  assign branch = opcode[3];

  // Notes on the sheet:
  //   0
  //   1
  //   2
  //   3
  //   0
  //   1
  //   2
  //   3
endmodule

module Control1 (
  input  [3:0] opcode,
  output ALUSrc,
  output MemtoReg,
  output RegWrite,
  output MemWrite,
  output branch,
  output jump,
  output extop,
  output Regdst,
  output ALUctr0,
  output ALUctr1,
  output ALUctr2,
  output ALUctr3
);

  wire and_2_out, and_3_out, and_4_out, and_7_out, and_8_out, and_10_out, and_11_out, and_12_out, and_13_out,
       not_1_out, not_2_out, not_3_out, not_4_out, not_5_out, not_6_out, not_7_out, not_8_out, not_9_out,
       not_10_out, not_11_out, not_12_out, not_13_out, not_14_out, not_15_out, not_16_out, not_17_out,
       not_18_out, not_19_out;

  or or_1 (ALUSrc, opcode[0], opcode[1], opcode[2]);
  and and_1 (MemtoReg, opcode[2], opcode[1], not_1_out);
  not not_1 (not_1_out, opcode[0]);
  not not_2 (not_2_out, opcode[3]);
  and and_2 (and_2_out, not_2_out, not_3_out);
  not not_3 (not_3_out, opcode[2]);
  not not_4 (not_4_out, opcode[3]);
  and and_3 (and_3_out, not_4_out, not_5_out);
  not not_5 (not_5_out, opcode[1]);
  not not_6 (not_6_out, opcode[3]);
  and and_4 (and_4_out, not_6_out, not_7_out);
  not not_7 (not_7_out, opcode[0]);
  and and_5 (MemWrite, opcode[2], opcode[1], opcode[0]);
  not not_8 (not_8_out, opcode[1]);
  and and_6 (jump, opcode[3], not_8_out, not_9_out);
  not not_9 (not_9_out, opcode[0]);
  not not_10 (not_10_out, opcode[1]);
  and and_7 (and_7_out, not_10_out, not_11_out);
  not not_11 (not_11_out, opcode[0]);
  and and_8 (and_8_out, opcode[2], opcode[1]);
  not not_12 (not_12_out, opcode[2]);
  and and_9 (Regdst, not_12_out, not_13_out, not_14_out);
  not not_13 (not_13_out, opcode[1]);
  not not_14 (not_14_out, opcode[0]);
  not not_15 (not_15_out, opcode[1]);
  and and_10 (and_10_out, not_15_out, opcode[0]);
  not not_16 (not_16_out, opcode[1]);
  and and_11 (and_11_out, not_16_out, not_17_out);
  not not_17 (not_17_out, opcode[0]);
  and and_12 (and_12_out, opcode[2], opcode[1]);
  not not_18 (not_18_out, opcode[2]);
  and and_13 (and_13_out, not_18_out, not_19_out);
  not not_19 (not_19_out, opcode[0]);
  or or_2 (RegWrite, and_2_out, and_3_out, and_4_out);
  or or_3 (extop, and_7_out, and_8_out, opcode[3]);
  or or_4 (ALUctr0, and_10_out, opcode[3]);
  or or_5 (ALUctr1, and_11_out, and_12_out);
  or or_6 (ALUctr3, and_13_out, opcode[3]);

  assign ALUctr2 = 1'b0;
  assign branch = opcode[3];
endmodule

module control2 (
  input  funct2,
  input  funct1,
  input  funct0,
  output ALUctr0,
  output ALUctr1,
  output ALUctr2,
  output ALUctr3
);


  assign ALUctr0 = 1'b0;
  assign ALUctr1 = funct2;
  assign ALUctr2 = funct1;
  assign ALUctr3 = funct0;
endmodule
